# Fritzing sketch CustomBootloader (saved by Fritzing 0.9.2b)
circuit board: 18.5863cm x 10.6812cm
perfboards: 1

parts:
  J1 = female pin header, 14 pins [form="♀ (female)"]
  J2 = female pin header, 14 pins [form="♀ (female)"]
  XTAL1 = CRYSTAL - kHz [frequency="16 MHz"]
  C1 = Capacitor [package=cap-pth-small2]
  C2 = Capacitor [package=cap-pth-small2]
  R4 = Resistor [tolerance=±5% resistance=10k package=THT]
  J3 = female pin header, 6 pins [form="♀ (female)"]
  Part1 = Arduino Uno (Rev3)  # not connected

nets (from the pcb view):
  N1: J1.pin1, R4.Pin_0, J3.pin6
  N2: J1.pin7, J2.pin9, R4.Pin_1, J3.pin2
  N3: J1.pin8, J2.pin7, C1.1, C2.2, J3.pin1
  N4: J1.pin9, XTAL1.pin_0, C1.2
  N5: J1.pin10, XTAL1.pin_1, C2.1
  N6: J2.pin10, J3.pin3
  N7: J2.pin11, J3.pin4
  N8: J2.pin12, J3.pin5

notes:
  Custom Bootloader
  Atmega IC
  +- 321 R
